# Fritzing sketch 5ladder (saved by Fritzing 0.9.3b)
breadboards: 1

parts:
  Part1 = Ethernet Pro
  LED1 = smd LED [color="Red (633nm)" package="0805 [SMD]"]
  LED3 = smd LED [color="Red (633nm)" package="0805 [SMD]"]
  LED4 = smd LED [color="Red (633nm)" package="0805 [SMD]"]
  LED5 = smd LED [color="Red (633nm)" package="0805 [SMD]"]
  LED6 = smd LED [color="Red (633nm)" package="0805 [SMD]"]
  R1 = Resistor [tolerance=±5% resistance=220 package=THT]
  R2 = Resistor [tolerance=±5% resistance=220 package=THT]
  R3 = Resistor [tolerance=±5% resistance=220 package=THT]
  R4 = Resistor [tolerance=±5% resistance=220 package=THT]
  R5 = Resistor [tolerance=±5% resistance=220 package=THT]

nets:
  N1: Part1.IO9, R3.Pin_0
  N2: Part1.*CS, R2.Pin_0
  N3: Part1.MISO, R1.Pin_0
  N4: Part1.GND, LED1.cathode, LED3.cathode, LED4.cathode, LED5.cathode, LED6.cathode
  N5: Part1.IO3, R5.Pin_0
  N6: Part1.IO5, R4.Pin_0
  N7: LED1.anode, R5.Pin_1
  N8: LED3.anode, R4.Pin_1
  N9: LED4.anode, R2.Pin_1
  N10: LED5.anode, R3.Pin_1
  N11: LED6.anode, R1.Pin_1

notes:
  5 ladder led
