# Fritzing sketch Fritz (saved by Fritzing 0.9.3b)
breadboards: 1

parts:
  Part1 = Arduino Mega 2560 (Rev3)
  LED1 = RGB LED (com. cathode, rbg) [package="5 mm [THT]"]

nets:
  N1: Part1.GND, LED1.blue_anode
  N2: Part1.D5_PWM, LED1.red_anode
  N3: Part1.D6_PWM, LED1.common_cathode
  N4: Part1.D7_PWM, LED1.green_anode
