# Fritzing sketch lemon (saved by Fritzing 0.9.3b)
breadboards: 1

parts:
  Part1 = Ethernet Pro
  LED2 = RGB LED (com. cathode, rgb) [package="5 mm [THT]"]
  LED3 = smd LED [color="Red (633nm)" package="0603 [SMD]"]
  LED4 = smd LED [color="Red (633nm)" package="0603 [SMD]"]
  LED5 = smd LED [color="Red (633nm)" package="0603 [SMD]"]
  LED6 = smd LED [color="Red (633nm)" package="0603 [SMD]"]
  LED7 = smd LED [color="Red (633nm)" package="0603 [SMD]"]
  R1 = Resistor [tolerance=±5% resistance=220 package="1206 [SMD]"]
  R3 = Resistor [tolerance=±5% resistance=220 package="1206 [SMD]"]
  R4 = Resistor [tolerance=±5% resistance=220 package="1206 [SMD]"]
  R5 = Resistor [tolerance=±5% resistance=220 package="1206 [SMD]"]
  R6 = Resistor [tolerance=±5% resistance=220 package="1206 [SMD]"]
  R7 = Resistor [tolerance=±5% resistance=220 package="1206 [SMD]"]
  R8 = Resistor [tolerance=±5% resistance=220 package="1206 [SMD]"]
  R9 = Resistor [tolerance=±5% resistance=220 package="1206 [SMD]"]
  J1 = Piezo Speaker
  R10 = Resistor [tolerance=±5% resistance=220 package="1206 [SMD]"]
  R11 = Photocell (LDR) [package=THT]

nets:
  N1: Part1.AD0, Part1.GND, LED2.common_cathode, LED3.anode, LED4.anode, LED5.anode, LED7.anode, J1.pin1, R11.pin_1
  N2: Part1.IO8, R3.Pin_0
  N3: Part1.IO9, R4.Pin_0
  N4: Part1.*CS, R5.Pin_0
  N5: Part1.MOSI, R6.Pin_0
  N6: Part1.MISO, R1.Pin_0
  N7: Part1.IO3, R7.Pin_0
  N8: Part1.IO5, R8.Pin_0
  N9: Part1.IO6, R9.Pin_0
  N10: Part1.5V, R10.Pin_0, R11.pin_0
  N11: LED2.red_anode, R9.Pin_1
  N12: LED2.green_anode, R8.Pin_1
  N13: LED2.blue_anode, R7.Pin_1
  N14: LED3.cathode, R1.Pin_1
  N15: LED4.cathode, R6.Pin_1
  N16: LED5.cathode, R4.Pin_1
  N17: LED6.cathode, R5.Pin_1
  N18: LED7.cathode, R3.Pin_1
  N19: J1.pin2, R10.Pin_1
