# Fritzing sketch lm358 (saved by Fritzing 0.9.3b)
breadboards: 1

parts:
  R1 = Photocell (LDR) [package=THT]
  Part1 = Ethernet Pro
  U1 = LM358 [package=dip08]
  R2 = Resistor [tolerance=±5% resistance=220 package="0402 [SMD]"]

nets (from the schematic view):
  N1: R1.pin_0, Part1.GND
  N2: R1.pin_1, Part1.AD0, R2.Pin_0
  N3: Part1.5V, U1.G$1_OUT
  N4: U1.G$1_V-, R2.Pin_1
