# Fritzing sketch photo (saved by Fritzing 0.9.3b)
breadboards: 1

parts:
  Part1 = Ethernet Pro
  LED1 = RGB LED (com. anode, rbg) [package="5 mm [THT]"]
  R1 = Resistor [tolerance=±5% resistance=220 package="0603 [SMD]"]
  R2 = Resistor [tolerance=±5% resistance=220 package="0402 [SMD]"]
  R3 = Resistor [tolerance=±5% resistance=220 package="0402 [SMD]"]
  R4 = Resistor [tolerance=±5% resistance=220 package="0402 [SMD]"]
  R5 = PHOTOCELL [package=photocell-kit]

nets:
  N1: Part1.AD0, R4.Pin_1, R5.P$1
  N2: Part1.GND, LED1.common_anode, R4.Pin_0
  N3: Part1.IO5, R1.Pin_1
  N4: Part1.IO6, R2.Pin_1
  N5: Part1.IO7, R3.Pin_1
  N6: Part1.5V, R5.P$2
  N7: LED1.red_cathode, R1.Pin_0
  N8: LED1.blue_cathode, R2.Pin_0
  N9: LED1.green_cathode, R3.Pin_0
