# Fritzing sketch thermin (saved by Fritzing 0.9.3b)
breadboards: 1

parts:
  Part1 = Arduino Uno (Rev3)
  R1 = Resistor [tolerance=±5% resistance=220 package=THT]
  R2 = PHOTOCELL [package=photocell]
  SG1 = Buzzer 12mm [package=buzzer-ccv-kit]

nets:
  N1: Part1.A0, R1.Pin_0, R2.P$1
  N2: Part1.GND, R1.Pin_1, SG1.1
  N3: Part1.D4, SG1.2
  N4: Part1.5V, R2.P$2
